// Digital circuit 16bitAdder.dig as structural Verilog
module _16bitAdder (
  input  Cin,
  input  B0,
  input  A0,
  input  B1,
  input  A1,
  input  B2,
  input  A2,
  input  B3,
  input  A3,
  input  B4,
  input  A4,
  input  B5,
  input  A5,
  input  B6,
  input  A6,
  input  B7,
  input  A7,
  input  B8,
  input  A8,
  input  B9,
  input  A9,
  input  B10,
  input  A10,
  input  B11,
  input  A11,
  input  B12,
  input  A12,
  input  B13,
  input  A13,
  input  B14,
  input  A14,
  input  B15,
  input  A15,
  output S0,
  output S1,
  output S2,
  output S3,
  output S4,
  output S5,
  output S6,
  output S7,
  output S8,
  output S9,
  output S10,
  output S11,
  output S12,
  output S13,
  output S14,
  output S15,
  output Cout
);

  wire and_1_out, and_2_out, and_3_out, and_4_out, and_5_out, and_6_out, and_7_out, and_8_out, and_9_out,
       and_10_out, and_11_out, and_12_out, and_13_out, and_14_out, and_15_out, and_16_out, and_17_out,
       and_18_out, and_19_out, and_20_out, and_21_out, and_22_out, and_23_out, and_24_out, and_25_out,
       and_26_out, and_27_out, and_28_out, and_29_out, and_30_out, and_31_out, and_32_out, and_33_out,
       and_34_out, and_35_out, and_36_out, and_37_out, and_38_out, and_39_out, and_40_out, and_41_out,
       and_42_out, and_43_out, and_44_out, and_45_out, and_46_out, and_47_out, and_48_out, and_49_out,
       and_50_out, and_51_out, and_52_out, and_53_out, and_54_out, and_55_out, and_56_out, and_57_out,
       and_58_out, and_59_out, and_60_out, and_61_out, and_62_out, and_63_out, and_64_out, and_65_out,
       and_66_out, and_67_out, and_68_out, and_69_out, and_70_out, and_71_out, and_72_out, and_73_out,
       and_74_out, and_75_out, and_76_out, and_77_out, and_78_out, and_79_out, and_80_out, and_81_out,
       and_82_out, and_83_out, and_84_out, and_85_out, and_86_out, and_87_out, and_88_out, and_89_out,
       and_90_out, and_91_out, and_92_out, and_93_out, and_94_out, and_95_out, and_96_out, or_1_out,
       or_2_out, or_3_out, or_4_out, or_5_out, or_6_out, or_7_out, or_8_out, or_9_out, or_10_out, or_11_out,
       or_12_out, or_13_out, or_14_out, or_15_out, or_16_out, or_17_out, or_18_out, or_19_out, or_20_out,
       or_21_out, or_22_out, or_23_out, or_24_out, or_25_out, or_26_out, or_27_out, or_28_out, or_29_out,
       or_30_out, or_31_out, or_32_out, or_33_out, or_34_out, or_35_out, or_36_out, or_38_out, or_39_out,
       or_40_out, xor_1_out, xor_2_out, xor_3_out, xor_4_out, xor_5_out, xor_6_out, xor_7_out, xor_8_out,
       xor_9_out, xor_10_out, xor_11_out, xor_12_out, xor_13_out, xor_14_out, xor_15_out, xor_16_out;

  xor xor_1 (xor_1_out, B15, A15);
  and and_1 (and_1_out, B15, A15);
  xor xor_2 (xor_2_out, B14, A14);
  and and_2 (and_2_out, B14, A14);
  xor xor_3 (xor_3_out, B13, A13);
  and and_3 (and_3_out, B13, A13);
  xor xor_4 (xor_4_out, B12, A12);
  and and_4 (and_4_out, B12, A12);
  xor xor_5 (xor_5_out, B11, A11);
  and and_5 (and_5_out, B11, A11);
  xor xor_6 (xor_6_out, B10, A10);
  and and_6 (and_6_out, B10, A10);
  xor xor_7 (xor_7_out, B9, A9);
  and and_7 (and_7_out, B9, A9);
  xor xor_8 (xor_8_out, B8, A8);
  and and_8 (and_8_out, B8, A8);
  xor xor_9 (xor_9_out, B7, A7);
  and and_9 (and_9_out, B7, A7);
  xor xor_10 (xor_10_out, B6, A6);
  and and_10 (and_10_out, B6, A6);
  xor xor_11 (xor_11_out, B5, A5);
  and and_11 (and_11_out, B5, A5);
  xor xor_12 (xor_12_out, B4, A4);
  and and_12 (and_12_out, B4, A4);
  xor xor_13 (xor_13_out, B3, A3);
  and and_13 (and_13_out, B3, A3);
  xor xor_14 (xor_14_out, B2, A2);
  and and_14 (and_14_out, B2, A2);
  xor xor_15 (xor_15_out, B1, A1);
  and and_15 (and_15_out, B1, A1);
  xor xor_16 (xor_16_out, B0, A0);
  and and_16 (and_16_out, B0, A0);
  and and_17 (and_17_out, xor_4_out, xor_3_out);
  and and_18 (and_18_out, xor_2_out, xor_1_out);
  and and_19 (and_19_out, and_4_out, xor_3_out);
  and and_20 (and_20_out, xor_2_out, xor_1_out);
  and and_21 (and_21_out, xor_2_out, xor_1_out);
  and and_22 (and_22_out, xor_1_out, and_2_out);
  and and_23 (and_23_out, or_38_out, xor_4_out);
  and and_24 (and_24_out, xor_3_out, xor_2_out);
  and and_25 (and_25_out, xor_3_out, xor_2_out);
  and and_26 (and_26_out, and_3_out, xor_2_out);
  and and_27 (and_27_out, xor_4_out, xor_3_out);
  and and_28 (and_28_out, and_4_out, xor_3_out);
  and and_29 (and_29_out, xor_4_out, or_38_out);
  and and_30 (and_30_out, xor_8_out, xor_7_out);
  and and_31 (and_31_out, xor_6_out, xor_5_out);
  and and_32 (and_32_out, and_8_out, xor_7_out);
  and and_33 (and_33_out, xor_6_out, xor_5_out);
  and and_34 (and_34_out, xor_6_out, xor_5_out);
  and and_35 (and_35_out, xor_5_out, and_6_out);
  and and_36 (and_36_out, or_39_out, xor_8_out);
  and and_37 (and_37_out, xor_7_out, xor_6_out);
  and and_38 (and_38_out, xor_7_out, xor_6_out);
  and and_39 (and_39_out, and_7_out, xor_6_out);
  and and_40 (and_40_out, xor_8_out, xor_7_out);
  and and_41 (and_41_out, and_8_out, xor_7_out);
  and and_42 (and_42_out, xor_8_out, or_39_out);
  and and_43 (and_43_out, xor_12_out, xor_11_out);
  and and_44 (and_44_out, xor_10_out, xor_9_out);
  and and_45 (and_45_out, and_12_out, xor_11_out);
  and and_46 (and_46_out, xor_10_out, xor_9_out);
  and and_47 (and_47_out, xor_10_out, xor_9_out);
  and and_48 (and_48_out, xor_9_out, and_10_out);
  and and_49 (and_49_out, or_40_out, xor_12_out);
  and and_50 (and_50_out, xor_11_out, xor_10_out);
  and and_51 (and_51_out, xor_11_out, xor_10_out);
  and and_52 (and_52_out, and_11_out, xor_10_out);
  and and_53 (and_53_out, xor_12_out, xor_11_out);
  and and_54 (and_54_out, and_12_out, xor_11_out);
  and and_55 (and_55_out, xor_12_out, or_40_out);
  and and_56 (and_56_out, xor_16_out, xor_15_out);
  and and_57 (and_57_out, xor_14_out, xor_13_out);
  and and_58 (and_58_out, and_16_out, xor_15_out);
  and and_59 (and_59_out, xor_14_out, xor_13_out);
  and and_60 (and_60_out, xor_14_out, xor_13_out);
  and and_61 (and_61_out, xor_13_out, and_14_out);
  and and_62 (and_62_out, Cin, xor_16_out);
  and and_63 (and_63_out, xor_15_out, xor_14_out);
  and and_64 (and_64_out, xor_15_out, xor_14_out);
  and and_65 (and_65_out, and_15_out, xor_14_out);
  and and_66 (and_66_out, xor_16_out, xor_15_out);
  and and_67 (and_67_out, and_16_out, xor_15_out);
  and and_68 (and_68_out, xor_16_out, Cin);
  and and_69 (and_69_out, or_38_out, and_17_out);
  and and_70 (and_70_out, and_19_out, and_20_out);
  and and_71 (and_71_out, and_21_out, and_3_out);
  and and_72 (and_72_out, and_23_out, and_24_out);
  and and_73 (and_73_out, and_25_out, and_4_out);
  or or_1 (or_1_out, and_26_out, and_2_out);
  and and_74 (and_74_out, and_27_out, or_38_out);
  or or_2 (or_2_out, and_28_out, and_3_out);
  and and_75 (and_75_out, or_39_out, and_30_out);
  and and_76 (and_76_out, and_32_out, and_33_out);
  and and_77 (and_77_out, and_34_out, and_7_out);
  and and_78 (and_78_out, and_36_out, and_37_out);
  and and_79 (and_79_out, and_38_out, and_8_out);
  or or_3 (or_3_out, and_39_out, and_6_out);
  and and_80 (and_80_out, and_40_out, or_39_out);
  or or_4 (or_4_out, and_41_out, and_7_out);
  and and_81 (and_81_out, or_40_out, and_43_out);
  and and_82 (and_82_out, and_45_out, and_46_out);
  and and_83 (and_83_out, and_47_out, and_11_out);
  and and_84 (and_84_out, and_49_out, and_50_out);
  and and_85 (and_85_out, and_51_out, and_12_out);
  or or_5 (or_5_out, and_52_out, and_10_out);
  and and_86 (and_86_out, and_53_out, or_40_out);
  or or_6 (or_6_out, and_54_out, and_11_out);
  and and_87 (and_87_out, Cin, and_56_out);
  and and_88 (and_88_out, and_58_out, and_59_out);
  and and_89 (and_89_out, and_60_out, and_15_out);
  and and_90 (and_90_out, and_62_out, and_63_out);
  and and_91 (and_91_out, and_64_out, and_16_out);
  or or_7 (or_7_out, and_65_out, and_14_out);
  and and_92 (and_92_out, and_66_out, Cin);
  or or_8 (or_8_out, and_67_out, and_15_out);
  or or_9 (or_9_out, and_29_out, and_4_out);
  or or_10 (or_10_out, and_42_out, and_8_out);
  or or_11 (or_11_out, and_55_out, and_12_out);
  or or_12 (or_12_out, and_68_out, and_16_out);
  and and_93 (and_93_out, and_69_out, and_18_out);
  or or_13 (or_13_out, and_72_out, and_73_out);
  or or_14 (or_14_out, and_74_out, or_2_out);
  and and_94 (and_94_out, and_75_out, and_31_out);
  or or_15 (or_15_out, and_78_out, and_79_out);
  or or_16 (or_16_out, and_80_out, or_4_out);
  and and_95 (and_95_out, and_81_out, and_44_out);
  or or_17 (or_17_out, and_84_out, and_85_out);
  or or_18 (or_18_out, and_86_out, or_6_out);
  and and_96 (and_96_out, and_87_out, and_57_out);
  or or_19 (or_19_out, and_90_out, and_91_out);
  or or_20 (or_20_out, and_92_out, or_8_out);
  or or_21 (or_21_out, and_93_out, and_70_out);
  or or_22 (or_22_out, and_71_out, and_22_out);
  or or_23 (or_23_out, or_13_out, or_1_out);
  or or_24 (or_24_out, and_94_out, and_76_out);
  or or_25 (or_25_out, and_77_out, and_35_out);
  or or_26 (or_26_out, or_15_out, or_3_out);
  or or_27 (or_27_out, and_95_out, and_82_out);
  or or_28 (or_28_out, and_83_out, and_48_out);
  or or_29 (or_29_out, or_17_out, or_5_out);
  or or_30 (or_30_out, and_96_out, and_88_out);
  or or_31 (or_31_out, and_89_out, and_61_out);
  or or_32 (or_32_out, or_19_out, or_7_out);
  or or_33 (or_33_out, or_22_out, and_1_out);
  or or_34 (or_34_out, or_25_out, and_5_out);
  or or_35 (or_35_out, or_28_out, and_9_out);
  or or_36 (or_36_out, or_31_out, and_13_out);
  xor xor_17 (S13, xor_3_out, or_9_out);
  xor xor_18 (S9, xor_7_out, or_10_out);
  xor xor_19 (S8, xor_8_out, or_39_out);
  xor xor_20 (S5, xor_11_out, or_11_out);
  xor xor_21 (S1, xor_15_out, or_12_out);
  xor xor_22 (S0, xor_16_out, Cin);
  or or_37 (Cout, or_21_out, or_33_out);
  xor xor_23 (S15, xor_1_out, or_23_out);
  xor xor_24 (S14, xor_2_out, or_14_out);
  xor xor_25 (S12, or_38_out, xor_4_out);
  or or_38 (or_38_out, or_24_out, or_34_out);
  xor xor_26 (S11, xor_5_out, or_26_out);
  xor xor_27 (S10, xor_6_out, or_16_out);
  or or_39 (or_39_out, or_27_out, or_35_out);
  xor xor_28 (S7, xor_9_out, or_29_out);
  xor xor_29 (S6, xor_10_out, or_18_out);
  xor xor_30 (S4, or_40_out, xor_12_out);
  or or_40 (or_40_out, or_30_out, or_36_out);
  xor xor_31 (S3, xor_13_out, or_32_out);
  xor xor_32 (S2, xor_14_out, or_20_out);
endmodule
