// Digital circuit 2'scomplement8bit.dig as structural Verilog
module _2_scomplement8bit (
  input  A0,
  input  A1,
  input  A2,
  input  A3,
  input  A4,
  input  A5,
  input  A6,
  input  A7,
  output S0,
  output S1,
  output S2,
  output S3,
  output S4,
  output S5,
  output S6,
  output S7,
  output Cout
);

  wire and_1_out, and_2_out, and_3_out, and_4_out, and_5_out, and_6_out, and_7_out, and_8_out, and_9_out,
       and_10_out, and_11_out, and_12_out, and_13_out, and_14_out, and_15_out, and_16_out, and_17_out,
       and_18_out, and_19_out, and_20_out, and_21_out, and_22_out, and_23_out, and_24_out, and_25_out,
       and_26_out, and_27_out, and_28_out, and_29_out, and_30_out, and_31_out, and_32_out, and_33_out,
       and_34_out, and_35_out, and_36_out, and_37_out, and_38_out, and_39_out, and_40_out, and_41_out,
       and_42_out, and_43_out, and_44_out, and_45_out, and_46_out, and_47_out, and_48_out, and_49_out,
       not_1_out, not_2_out, not_3_out, not_4_out, not_5_out, not_6_out, not_7_out, not_8_out, not_9_out,
       not_10_out, or_1_out, or_2_out, or_3_out, or_4_out, or_5_out, or_6_out, or_7_out, or_8_out, or_9_out,
       or_10_out, or_11_out, or_12_out, or_13_out, or_14_out, or_15_out, or_16_out, or_17_out, or_18_out,
       or_20_out, xor_1_out, xor_2_out, xor_3_out, xor_4_out, xor_5_out, xor_6_out, xor_7_out, xor_8_out;

  not not_1 (not_1_out, A7);
  not not_2 (not_2_out, A6);
  not not_3 (not_3_out, A5);
  not not_4 (not_4_out, A4);
  not not_5 (not_5_out, A3);
  not not_6 (not_6_out, A2);
  not not_7 (not_7_out, A1);
  not not_8 (not_8_out, A0);
  not not_9 (not_9_out, not_1_out);
  and and_1 (and_1_out, not_9_out, not_1_out);
  not not_10 (not_10_out, and_1_out);
  and and_2 (and_2_out, and_1_out, not_1_out);
  and and_3 (and_3_out, and_1_out, not_2_out);
  and and_4 (and_4_out, and_1_out, not_3_out);
  and and_5 (and_5_out, and_1_out, not_4_out);
  and and_6 (and_6_out, and_1_out, not_5_out);
  and and_7 (and_7_out, and_1_out, not_6_out);
  and and_8 (and_8_out, and_1_out, not_7_out);
  and and_9 (and_9_out, and_1_out, not_8_out);
  xor xor_1 (xor_1_out, and_1_out, not_1_out);
  xor xor_2 (xor_2_out, and_1_out, not_2_out);
  xor xor_3 (xor_3_out, and_1_out, not_3_out);
  xor xor_4 (xor_4_out, and_1_out, not_4_out);
  xor xor_5 (xor_5_out, and_1_out, not_5_out);
  xor xor_6 (xor_6_out, and_1_out, not_6_out);
  xor xor_7 (xor_7_out, and_1_out, not_7_out);
  xor xor_8 (xor_8_out, and_1_out, not_8_out);
  and and_10 (and_10_out, xor_4_out, xor_3_out);
  and and_11 (and_11_out, xor_2_out, xor_1_out);
  and and_12 (and_12_out, and_5_out, xor_3_out);
  and and_13 (and_13_out, xor_2_out, xor_1_out);
  and and_14 (and_14_out, xor_2_out, xor_1_out);
  and and_15 (and_15_out, xor_1_out, and_3_out);
  and and_16 (and_16_out, or_20_out, xor_4_out);
  and and_17 (and_17_out, xor_3_out, xor_2_out);
  and and_18 (and_18_out, xor_3_out, xor_2_out);
  and and_19 (and_19_out, and_4_out, xor_2_out);
  and and_20 (and_20_out, xor_4_out, xor_3_out);
  and and_21 (and_21_out, and_5_out, xor_3_out);
  and and_22 (and_22_out, xor_4_out, or_20_out);
  and and_23 (and_23_out, xor_8_out, xor_7_out);
  and and_24 (and_24_out, xor_6_out, xor_5_out);
  and and_25 (and_25_out, and_9_out, xor_7_out);
  and and_26 (and_26_out, xor_6_out, xor_5_out);
  and and_27 (and_27_out, xor_6_out, xor_5_out);
  and and_28 (and_28_out, xor_5_out, and_7_out);
  and and_29 (and_29_out, not_10_out, xor_8_out);
  and and_30 (and_30_out, xor_7_out, xor_6_out);
  and and_31 (and_31_out, xor_7_out, xor_6_out);
  and and_32 (and_32_out, and_8_out, xor_6_out);
  and and_33 (and_33_out, xor_8_out, xor_7_out);
  and and_34 (and_34_out, and_9_out, xor_7_out);
  and and_35 (and_35_out, xor_8_out, not_10_out);
  and and_36 (and_36_out, or_20_out, and_10_out);
  and and_37 (and_37_out, and_12_out, and_13_out);
  and and_38 (and_38_out, and_14_out, and_4_out);
  and and_39 (and_39_out, and_16_out, and_17_out);
  and and_40 (and_40_out, and_18_out, and_5_out);
  or or_1 (or_1_out, and_19_out, and_3_out);
  and and_41 (and_41_out, and_20_out, or_20_out);
  or or_2 (or_2_out, and_21_out, and_4_out);
  and and_42 (and_42_out, not_10_out, and_23_out);
  and and_43 (and_43_out, and_25_out, and_26_out);
  and and_44 (and_44_out, and_27_out, and_8_out);
  and and_45 (and_45_out, and_29_out, and_30_out);
  and and_46 (and_46_out, and_31_out, and_9_out);
  or or_3 (or_3_out, and_32_out, and_7_out);
  and and_47 (and_47_out, and_33_out, not_10_out);
  or or_4 (or_4_out, and_34_out, and_8_out);
  or or_5 (or_5_out, and_22_out, and_5_out);
  or or_6 (or_6_out, and_35_out, and_9_out);
  and and_48 (and_48_out, and_36_out, and_11_out);
  or or_7 (or_7_out, and_39_out, and_40_out);
  or or_8 (or_8_out, and_41_out, or_2_out);
  and and_49 (and_49_out, and_42_out, and_24_out);
  or or_9 (or_9_out, and_45_out, and_46_out);
  or or_10 (or_10_out, and_47_out, or_4_out);
  or or_11 (or_11_out, and_48_out, and_37_out);
  or or_12 (or_12_out, and_38_out, and_15_out);
  or or_13 (or_13_out, or_7_out, or_1_out);
  or or_14 (or_14_out, and_49_out, and_43_out);
  or or_15 (or_15_out, and_44_out, and_28_out);
  or or_16 (or_16_out, or_9_out, or_3_out);
  or or_17 (or_17_out, or_12_out, and_2_out);
  or or_18 (or_18_out, or_15_out, and_6_out);
  xor xor_9 (S6, xor_2_out, or_8_out);
  xor xor_10 (S5, xor_3_out, or_5_out);
  xor xor_11 (S4, or_20_out, xor_4_out);
  xor xor_12 (S2, xor_6_out, or_10_out);
  xor xor_13 (S1, xor_7_out, or_6_out);
  xor xor_14 (S0, xor_8_out, not_10_out);
  or or_19 (Cout, or_11_out, or_17_out);
  xor xor_15 (S7, xor_1_out, or_13_out);
  or or_20 (or_20_out, or_14_out, or_18_out);
  xor xor_16 (S3, xor_5_out, or_16_out);
endmodule
