// Digital circuit divider.dig as structural Verilog
module divider (
  input  A0,
  input  A1,
  input  A2,
  input  A3,
  input  A4,
  input  A5,
  input  A6,
  input  A7,
  input  B0,
  input  B1,
  input  B2,
  input  B3,
  input  B4,
  input  B5,
  input  B6,
  input  B7,
  output Q0,
  output Q1,
  output Q2,
  output Q3,
  output Q4,
  output Q5,
  output Q6,
  output Q7,
  output R0,
  output R1,
  output R2,
  output R3,
  output R4,
  output R5,
  output R6,
  output R7
);

  wire and_1_out, mux_2_out, mux_3_out, mux_4_out, mux_5_out, mux_6_out, mux_7_out, mux_8_out, mux_10_out,
       mux_11_out, mux_12_out, mux_13_out, mux_14_out, mux_15_out, mux_16_out, mux_18_out, mux_19_out,
       mux_20_out, mux_21_out, mux_22_out, mux_23_out, mux_24_out, mux_26_out, mux_27_out, mux_28_out,
       mux_29_out, mux_30_out, mux_31_out, mux_32_out, mux_34_out, mux_35_out, mux_36_out, mux_37_out,
       mux_38_out, mux_39_out, mux_40_out, mux_42_out, mux_43_out, mux_44_out, mux_45_out, mux_46_out,
       mux_47_out, mux_48_out, mux_50_out, mux_51_out, mux_52_out, mux_53_out, mux_54_out, mux_55_out,
       mux_56_out, not_1_out, subtractor8bit_1_s0, subtractor8bit_1_s1, subtractor8bit_1_s2,
       subtractor8bit_1_s3, subtractor8bit_1_s4, subtractor8bit_1_s5, subtractor8bit_1_s6,
       subtractor8bit_1_s7, subtractor8bit_2_s0, subtractor8bit_2_s1, subtractor8bit_2_s2,
       subtractor8bit_2_s3, subtractor8bit_2_s4, subtractor8bit_2_s5, subtractor8bit_2_s6,
       subtractor8bit_2_s7, subtractor8bit_3_s0, subtractor8bit_3_s1, subtractor8bit_3_s2,
       subtractor8bit_3_s3, subtractor8bit_3_s4, subtractor8bit_3_s5, subtractor8bit_3_s6,
       subtractor8bit_3_s7, subtractor8bit_4_s0, subtractor8bit_4_s1, subtractor8bit_4_s2,
       subtractor8bit_4_s3, subtractor8bit_4_s4, subtractor8bit_4_s5, subtractor8bit_4_s6,
       subtractor8bit_4_s7, subtractor8bit_5_s0, subtractor8bit_5_s1, subtractor8bit_5_s2,
       subtractor8bit_5_s3, subtractor8bit_5_s4, subtractor8bit_5_s5, subtractor8bit_5_s6,
       subtractor8bit_5_s7, subtractor8bit_6_s0, subtractor8bit_6_s1, subtractor8bit_6_s2,
       subtractor8bit_6_s3, subtractor8bit_6_s4, subtractor8bit_6_s5, subtractor8bit_6_s6,
       subtractor8bit_6_s7, subtractor8bit_7_s0, subtractor8bit_7_s1, subtractor8bit_7_s2,
       subtractor8bit_7_s3, subtractor8bit_7_s4, subtractor8bit_7_s5, subtractor8bit_7_s6,
       subtractor8bit_7_s7, subtractor8bit_8_s0, subtractor8bit_8_s1, subtractor8bit_8_s2,
       subtractor8bit_8_s3, subtractor8bit_8_s4, subtractor8bit_8_s5, subtractor8bit_8_s6,
       subtractor8bit_8_s7;

  mux mux_1 (.I1(subtractor8bit_1_s7), .A(Q7), .I0(and_1_out));  // open: OUT
  mux mux_2 (.I1(subtractor8bit_1_s6), .A(Q7), .I0(and_1_out), .OUT(mux_2_out));
  mux mux_3 (.I1(subtractor8bit_1_s5), .A(Q7), .I0(and_1_out), .OUT(mux_3_out));
  mux mux_4 (.I1(subtractor8bit_1_s4), .A(Q7), .I0(and_1_out), .OUT(mux_4_out));
  not not_1 (not_1_out, B0);
  and and_1 (and_1_out, B0, not_1_out);
  mux mux_5 (.I1(subtractor8bit_1_s3), .A(Q7), .I0(and_1_out), .OUT(mux_5_out));
  subtractor8bit subtractor8bit_1 (
    .B0(B0), .A0(A7), .B1(B1), .A1(and_1_out), .B2(B2), .A2(and_1_out), .B3(B3), .A3(and_1_out), .B4(B4),
    .A4(and_1_out), .B5(B5), .A5(and_1_out), .B6(B6), .A6(and_1_out), .B7(B7), .A7(and_1_out),
    .S0(subtractor8bit_1_s0), .S1(subtractor8bit_1_s1), .S2(subtractor8bit_1_s2), .S3(subtractor8bit_1_s3),
    .S4(subtractor8bit_1_s4), .S5(subtractor8bit_1_s5), .S6(subtractor8bit_1_s6), .S7(subtractor8bit_1_s7),
    .Cout(Q7));
  mux mux_6 (.I1(subtractor8bit_1_s2), .A(Q7), .I0(and_1_out), .OUT(mux_6_out));
  mux mux_7 (.I1(subtractor8bit_1_s1), .A(Q7), .I0(and_1_out), .OUT(mux_7_out));
  mux mux_8 (.I1(subtractor8bit_1_s0), .A(Q7), .I0(A7), .OUT(mux_8_out));
  mux mux_9 (.I1(subtractor8bit_2_s7), .A(Q6), .I0(mux_2_out));  // open: OUT
  mux mux_10 (.I1(subtractor8bit_2_s6), .A(Q6), .I0(mux_3_out), .OUT(mux_10_out));
  mux mux_11 (.I1(subtractor8bit_2_s5), .A(Q6), .I0(mux_4_out), .OUT(mux_11_out));
  mux mux_12 (.I1(subtractor8bit_2_s4), .A(Q6), .I0(mux_5_out), .OUT(mux_12_out));
  mux mux_13 (.I1(subtractor8bit_2_s3), .A(Q6), .I0(mux_6_out), .OUT(mux_13_out));
  subtractor8bit subtractor8bit_2 (
    .B0(B0), .A0(A6), .B1(B1), .A1(mux_8_out), .B2(B2), .A2(mux_7_out), .B3(B3), .A3(mux_6_out), .B4(B4),
    .A4(mux_5_out), .B5(B5), .A5(mux_4_out), .B6(B6), .A6(mux_3_out), .B7(B7), .A7(mux_2_out),
    .S0(subtractor8bit_2_s0), .S1(subtractor8bit_2_s1), .S2(subtractor8bit_2_s2), .S3(subtractor8bit_2_s3),
    .S4(subtractor8bit_2_s4), .S5(subtractor8bit_2_s5), .S6(subtractor8bit_2_s6), .S7(subtractor8bit_2_s7),
    .Cout(Q6));
  mux mux_14 (.I1(subtractor8bit_2_s2), .A(Q6), .I0(mux_7_out), .OUT(mux_14_out));
  mux mux_15 (.I1(subtractor8bit_2_s1), .A(Q6), .I0(mux_8_out), .OUT(mux_15_out));
  mux mux_16 (.I1(subtractor8bit_2_s0), .A(Q6), .I0(A6), .OUT(mux_16_out));
  mux mux_17 (.I1(subtractor8bit_3_s7), .A(Q5), .I0(mux_10_out));  // open: OUT
  mux mux_18 (.I1(subtractor8bit_3_s6), .A(Q5), .I0(mux_11_out), .OUT(mux_18_out));
  mux mux_19 (.I1(subtractor8bit_3_s5), .A(Q5), .I0(mux_12_out), .OUT(mux_19_out));
  mux mux_20 (.I1(subtractor8bit_3_s4), .A(Q5), .I0(mux_13_out), .OUT(mux_20_out));
  mux mux_21 (.I1(subtractor8bit_3_s3), .A(Q5), .I0(mux_14_out), .OUT(mux_21_out));
  subtractor8bit subtractor8bit_3 (
    .B0(B0), .A0(A5), .B1(B1), .A1(mux_16_out), .B2(B2), .A2(mux_15_out), .B3(B3), .A3(mux_14_out), .B4(B4),
    .A4(mux_13_out), .B5(B5), .A5(mux_12_out), .B6(B6), .A6(mux_11_out), .B7(B7), .A7(mux_10_out),
    .S0(subtractor8bit_3_s0), .S1(subtractor8bit_3_s1), .S2(subtractor8bit_3_s2), .S3(subtractor8bit_3_s3),
    .S4(subtractor8bit_3_s4), .S5(subtractor8bit_3_s5), .S6(subtractor8bit_3_s6), .S7(subtractor8bit_3_s7),
    .Cout(Q5));
  mux mux_22 (.I1(subtractor8bit_3_s2), .A(Q5), .I0(mux_15_out), .OUT(mux_22_out));
  mux mux_23 (.I1(subtractor8bit_3_s1), .A(Q5), .I0(mux_16_out), .OUT(mux_23_out));
  mux mux_24 (.I1(subtractor8bit_3_s0), .A(Q5), .I0(A5), .OUT(mux_24_out));
  mux mux_25 (.I1(subtractor8bit_4_s7), .A(Q4), .I0(mux_18_out));  // open: OUT
  mux mux_26 (.I1(subtractor8bit_4_s6), .A(Q4), .I0(mux_19_out), .OUT(mux_26_out));
  mux mux_27 (.I1(subtractor8bit_4_s5), .A(Q4), .I0(mux_20_out), .OUT(mux_27_out));
  mux mux_28 (.I1(subtractor8bit_4_s4), .A(Q4), .I0(mux_21_out), .OUT(mux_28_out));
  mux mux_29 (.I1(subtractor8bit_4_s3), .A(Q4), .I0(mux_22_out), .OUT(mux_29_out));
  subtractor8bit subtractor8bit_4 (
    .B0(B0), .A0(A4), .B1(B1), .A1(mux_24_out), .B2(B2), .A2(mux_23_out), .B3(B3), .A3(mux_22_out), .B4(B4),
    .A4(mux_21_out), .B5(B5), .A5(mux_20_out), .B6(B6), .A6(mux_19_out), .B7(B7), .A7(mux_18_out),
    .S0(subtractor8bit_4_s0), .S1(subtractor8bit_4_s1), .S2(subtractor8bit_4_s2), .S3(subtractor8bit_4_s3),
    .S4(subtractor8bit_4_s4), .S5(subtractor8bit_4_s5), .S6(subtractor8bit_4_s6), .S7(subtractor8bit_4_s7),
    .Cout(Q4));
  mux mux_30 (.I1(subtractor8bit_4_s2), .A(Q4), .I0(mux_23_out), .OUT(mux_30_out));
  mux mux_31 (.I1(subtractor8bit_4_s1), .A(Q4), .I0(mux_24_out), .OUT(mux_31_out));
  mux mux_32 (.I1(subtractor8bit_4_s0), .A(Q4), .I0(A4), .OUT(mux_32_out));
  mux mux_33 (.I1(subtractor8bit_5_s7), .A(Q3), .I0(mux_26_out));  // open: OUT
  mux mux_34 (.I1(subtractor8bit_5_s6), .A(Q3), .I0(mux_27_out), .OUT(mux_34_out));
  mux mux_35 (.I1(subtractor8bit_5_s5), .A(Q3), .I0(mux_28_out), .OUT(mux_35_out));
  mux mux_36 (.I1(subtractor8bit_5_s4), .A(Q3), .I0(mux_29_out), .OUT(mux_36_out));
  mux mux_37 (.I1(subtractor8bit_5_s3), .A(Q3), .I0(mux_30_out), .OUT(mux_37_out));
  subtractor8bit subtractor8bit_5 (
    .B0(B0), .A0(A3), .B1(B1), .A1(mux_32_out), .B2(B2), .A2(mux_31_out), .B3(B3), .A3(mux_30_out), .B4(B4),
    .A4(mux_29_out), .B5(B5), .A5(mux_28_out), .B6(B6), .A6(mux_27_out), .B7(B7), .A7(mux_26_out),
    .S0(subtractor8bit_5_s0), .S1(subtractor8bit_5_s1), .S2(subtractor8bit_5_s2), .S3(subtractor8bit_5_s3),
    .S4(subtractor8bit_5_s4), .S5(subtractor8bit_5_s5), .S6(subtractor8bit_5_s6), .S7(subtractor8bit_5_s7),
    .Cout(Q3));
  mux mux_38 (.I1(subtractor8bit_5_s2), .A(Q3), .I0(mux_31_out), .OUT(mux_38_out));
  mux mux_39 (.I1(subtractor8bit_5_s1), .A(Q3), .I0(mux_32_out), .OUT(mux_39_out));
  mux mux_40 (.I1(subtractor8bit_5_s0), .A(Q3), .I0(A3), .OUT(mux_40_out));
  mux mux_41 (.I1(subtractor8bit_6_s7), .A(Q2), .I0(mux_34_out));  // open: OUT
  mux mux_42 (.I1(subtractor8bit_6_s6), .A(Q2), .I0(mux_35_out), .OUT(mux_42_out));
  mux mux_43 (.I1(subtractor8bit_6_s5), .A(Q2), .I0(mux_36_out), .OUT(mux_43_out));
  mux mux_44 (.I1(subtractor8bit_6_s4), .A(Q2), .I0(mux_37_out), .OUT(mux_44_out));
  mux mux_45 (.I1(subtractor8bit_6_s3), .A(Q2), .I0(mux_38_out), .OUT(mux_45_out));
  subtractor8bit subtractor8bit_6 (
    .B0(B0), .A0(A2), .B1(B1), .A1(mux_40_out), .B2(B2), .A2(mux_39_out), .B3(B3), .A3(mux_38_out), .B4(B4),
    .A4(mux_37_out), .B5(B5), .A5(mux_36_out), .B6(B6), .A6(mux_35_out), .B7(B7), .A7(mux_34_out),
    .S0(subtractor8bit_6_s0), .S1(subtractor8bit_6_s1), .S2(subtractor8bit_6_s2), .S3(subtractor8bit_6_s3),
    .S4(subtractor8bit_6_s4), .S5(subtractor8bit_6_s5), .S6(subtractor8bit_6_s6), .S7(subtractor8bit_6_s7),
    .Cout(Q2));
  mux mux_46 (.I1(subtractor8bit_6_s2), .A(Q2), .I0(mux_39_out), .OUT(mux_46_out));
  mux mux_47 (.I1(subtractor8bit_6_s1), .A(Q2), .I0(mux_40_out), .OUT(mux_47_out));
  mux mux_48 (.I1(subtractor8bit_6_s0), .A(Q2), .I0(A2), .OUT(mux_48_out));
  mux mux_49 (.I1(subtractor8bit_7_s7), .A(Q1), .I0(mux_42_out));  // open: OUT
  mux mux_50 (.I1(subtractor8bit_7_s6), .A(Q1), .I0(mux_43_out), .OUT(mux_50_out));
  mux mux_51 (.I1(subtractor8bit_7_s5), .A(Q1), .I0(mux_44_out), .OUT(mux_51_out));
  mux mux_52 (.I1(subtractor8bit_7_s4), .A(Q1), .I0(mux_45_out), .OUT(mux_52_out));
  mux mux_53 (.I1(subtractor8bit_7_s3), .A(Q1), .I0(mux_46_out), .OUT(mux_53_out));
  subtractor8bit subtractor8bit_7 (
    .B0(B0), .A0(A1), .B1(B1), .A1(mux_48_out), .B2(B2), .A2(mux_47_out), .B3(B3), .A3(mux_46_out), .B4(B4),
    .A4(mux_45_out), .B5(B5), .A5(mux_44_out), .B6(B6), .A6(mux_43_out), .B7(B7), .A7(mux_42_out),
    .S0(subtractor8bit_7_s0), .S1(subtractor8bit_7_s1), .S2(subtractor8bit_7_s2), .S3(subtractor8bit_7_s3),
    .S4(subtractor8bit_7_s4), .S5(subtractor8bit_7_s5), .S6(subtractor8bit_7_s6), .S7(subtractor8bit_7_s7),
    .Cout(Q1));
  mux mux_54 (.I1(subtractor8bit_7_s2), .A(Q1), .I0(mux_47_out), .OUT(mux_54_out));
  mux mux_55 (.I1(subtractor8bit_7_s1), .A(Q1), .I0(mux_48_out), .OUT(mux_55_out));
  mux mux_56 (.I1(subtractor8bit_7_s0), .A(Q1), .I0(A1), .OUT(mux_56_out));
  mux mux_57 (.I1(subtractor8bit_8_s7), .A(Q0), .I0(mux_50_out), .OUT(R7));
  mux mux_58 (.I1(subtractor8bit_8_s6), .A(Q0), .I0(mux_51_out), .OUT(R6));
  mux mux_59 (.I1(subtractor8bit_8_s5), .A(Q0), .I0(mux_52_out), .OUT(R5));
  mux mux_60 (.I1(subtractor8bit_8_s4), .A(Q0), .I0(mux_53_out), .OUT(R4));
  mux mux_61 (.I1(subtractor8bit_8_s3), .A(Q0), .I0(mux_54_out), .OUT(R3));
  subtractor8bit subtractor8bit_8 (
    .B0(B0), .A0(A0), .B1(B1), .A1(mux_56_out), .B2(B2), .A2(mux_55_out), .B3(B3), .A3(mux_54_out), .B4(B4),
    .A4(mux_53_out), .B5(B5), .A5(mux_52_out), .B6(B6), .A6(mux_51_out), .B7(B7), .A7(mux_50_out),
    .S0(subtractor8bit_8_s0), .S1(subtractor8bit_8_s1), .S2(subtractor8bit_8_s2), .S3(subtractor8bit_8_s3),
    .S4(subtractor8bit_8_s4), .S5(subtractor8bit_8_s5), .S6(subtractor8bit_8_s6), .S7(subtractor8bit_8_s7),
    .Cout(Q0));
  mux mux_62 (.I1(subtractor8bit_8_s2), .A(Q0), .I0(mux_55_out), .OUT(R2));
  mux mux_63 (.I1(subtractor8bit_8_s1), .A(Q0), .I0(mux_56_out), .OUT(R1));
  mux mux_64 (.I1(subtractor8bit_8_s0), .A(Q0), .I0(A0), .OUT(R0));
endmodule
