// Digital circuit mux.dig as structural Verilog
module mux (
  input  I1,
  input  A,
  input  I0,
  output OUT
);

  wire and_1_out, and_2_out, not_1_out;

  not not_1 (not_1_out, A);
  and and_1 (and_1_out, I0, not_1_out);
  and and_2 (and_2_out, I1, A);
  or or_1 (OUT, and_1_out, and_2_out);
endmodule
